# Fritzing sketch DriveboardUSB (saved by Fritzing 0.9.3b)
stripboards: 8

parts:
  Part1 = Arduino Uno (Rev3)
  D1 = Rectifier Diode [part_number=1N4001 package="300 mil [THT]"]
  JACK1 = ETHERNET-JACK-90 [part_number=RJHSE3381A1]
  IC3 = SO08-EIAJ [chip_label=064L part_number=ACPL-064L-000E package=SO]
  J1 = male pin header, 12 pins [form="♂ (male)"]
  J2 = male pin header, 12 pins [form="♂ (male)"]
  JACK2 = ETHERNET-JACK-90 [part_number=RJHSE3381A1]
  IC4 = SO08-EIAJ [chip_label=064L part_number=ACPL-064L-000E package=SO]
  JACK3 = ETHERNET-JACK-90 [part_number=RJHSE3381A1]
  IC5 = SO08-EIAJ [chip_label=064L part_number=ACPL-064L-000E package=SO]
  JACK4 = ETHERNET-JACK-90 [part_number=RJHSE3381A1]
  JACK5 = ETHERNET-JACK-90 [part_number=RJHSE3381A1]
  JACK6 = ETHERNET-JACK-90 [part_number=RJHSE3381A1]
  24V = Power Jack [part_number=PJ-002AH-SMT-TR package=power_jack_smd]
  5V = Power Jack [part_number=PJ-002AH-SMT-TR package=power_jack_smd]
  R20 = Resistor [tolerance=±1% resistance=845 package="1206 [SMD]"]
  R21 = Resistor [tolerance=±1% resistance=845 package="1206 [SMD]"]
  R22 = Resistor [tolerance=±1% resistance=845 package="1206 [SMD]"]
  R23 = Resistor [tolerance=±1% resistance=845 package="1206 [SMD]"]
  R24 = Resistor [tolerance=±1% resistance=845 package="1206 [SMD]"]
  R25 = Resistor [tolerance=±1% resistance=845 package="1206 [SMD]"]
  R26 = Resistor [tolerance=±1% resistance=845 package="1206 [SMD]"]
  R27 = Resistor [tolerance=±1% resistance=845 package="1206 [SMD]"]
  R28 = Resistor [tolerance=±1% resistance=845 package="1206 [SMD]"]
  R29 = Resistor [tolerance=±1% resistance=845 package="1206 [SMD]"]
  R30 = Resistor [tolerance=±1% resistance=845 package="1206 [SMD]"]
  R31 = Resistor [tolerance=±1% resistance=845 package="1206 [SMD]"]
  JACK7 = ETHERNET-JACK-90 [part_number=RJHSE3381A1]
  JACK9 = ETHERNET-JACK-90 [part_number=RJHSE3381A1]
  JACK10 = ETHERNET-JACK-90 [part_number=RJHSE3381A1]
  JACK11 = ETHERNET-JACK-90 [part_number=RJHSE3381A1]
  JACK12 = ETHERNET-JACK-90 [part_number=RJHSE3381A1]
  IC7 = SO08-EIAJ [chip_label=064L part_number=ACPL-064L-000E package=SO]
  IC8 = SO08-EIAJ [chip_label=064L part_number=ACPL-064L-000E package=SO]
  R32 = Resistor [tolerance=±1% resistance=845 package="1206 [SMD]"]
  R36 = Resistor [tolerance=±1% resistance=845 package="1206 [SMD]"]
  R40 = Resistor [tolerance=±1% resistance=845 package="1206 [SMD]"]
  R41 = Resistor [tolerance=±1% resistance=845 package="1206 [SMD]"]
  R42 = Resistor [tolerance=±1% resistance=845 package="1206 [SMD]"]
  R43 = Resistor [tolerance=±1% resistance=845 package="1206 [SMD]"]
  R44 = Resistor [tolerance=±1% resistance=10k package="1206 [SMD]"]
  R45 = Resistor [tolerance=±1% resistance=10k package="1206 [SMD]"]
  air_asssist_ssr = IC, DIP package, 4 pins [chip_label=SSR]
  air_asssist_ssr1 = IC, DIP package, 4 pins [chip_label=SSR]
  R46 = Resistor [tolerance=±1% resistance=845 package="1206 [SMD]"]
  IC9 = SO08-EIAJ [chip_label=064L part_number=ACPL-064L-000E package=SO]
  R47 = Resistor [tolerance=±1% resistance=845 package="1206 [SMD]"]
  R48 = Resistor [tolerance=±1% resistance=845 package="1206 [SMD]"]
  R49 = Resistor [tolerance=±1% resistance=845 package="1206 [SMD]"]
  R50 = Resistor [tolerance=±1% resistance=845 package="1206 [SMD]"]
  R51 = Resistor [tolerance=±1% resistance=845 package="1206 [SMD]"]
  C1 = Ceramic Capacitor [capacitance=0.1µF voltage=16V package="1206 [SMD, multilayer]"]
  C2 = Ceramic Capacitor [capacitance=0.1µF voltage=16V package="1206 [SMD, multilayer]"]
  C3 = Ceramic Capacitor [capacitance=0.1µF voltage=16V package="1206 [SMD, multilayer]"]
  C4 = Ceramic Capacitor [capacitance=0.1µF voltage=16V package="1206 [SMD, multilayer]"]
  C5 = Ceramic Capacitor [capacitance=0.1µF voltage=16V package="1206 [SMD, multilayer]"]
  C6 = Ceramic Capacitor [capacitance=0.1µF voltage=16V package="1206 [SMD, multilayer]"]
  J3 = male pin header, 12 pins [form="♂ (male)"]
  JACK13 = ETHERNET-JACK-90 [part_number=RJHSE3381A1]
  JACK14 = ETHERNET-JACK-90 [part_number=RJHSE3381A1]
  JACK15 = ETHERNET-JACK-90 [part_number=RJHSE3381A1]

nets:
  N1: Part1.A0, IC3.7
  N2: Part1.A1, IC3.6
  N3: Part1.A2, IC4.7, IC8.7
  N4: Part1.A3, IC4.6
  N5: Part1.A4/SDA, IC5.7
  N6: Part1.A5/SCL, IC5.6
  N7: Part1.D8, J1.pin9
  N8: Part1.D9_PWM, J2.pin9
  N9: Part1.D10_PWM/SS, J3.pin9
  N10: Part1.D11_PWM/MOSI, J1.pin8
  N11: Part1.D12/MISO, J2.pin8
  N12: Part1.D13/SCK, J3.pin8
  N13: Part1.GND, IC3.5, J1.pin10, J2.pin10, IC4.5, IC5.5, IC8.5, R43.Pin_1, air_asssist_ssr.pin2, air_asssist_ssr1.pin2, IC9.5, C1.0, C2.0, C3.0, C5.0, C6.0, J3.pin10
  N14: Part1.D2, IC9.6
  N15: Part1.D3_PWM, IC8.6, R41.Pin_1
  N16: Part1.D4, R51.Pin_0
  N17: Part1.D5_PWM, R36.Pin_1
  N18: Part1.D6_PWM, R46.Pin_1
  N19: Part1.D7, IC9.7
  N20: Part1.5V, IC3.8, IC4.8, IC5.8, IC8.8, R42.Pin_1, IC9.8, C1.1, C2.1, C3.1, C5.1, C6.1
  N21: D1.cathode, JACK11.1, JACK11.3, JACK11.GLED-, JACK11.GLED+, air_asssist_ssr.pin3
  N22: D1.anode, J1.pin1, J2.pin1, 24V.GND, 24V.GNDBREAK, JACK11.2, JACK11.6, JACK11.7, JACK11.8, J3.pin1
  N23: JACK1.1, JACK1.3, JACK1.GLED+, JACK2.1, JACK2.3, JACK2.GLED+, JACK3.1, JACK3.3, JACK4.1, JACK4.3, JACK4.GLED+, JACK5.1, JACK5.3, JACK6.1, JACK6.3
  N24: JACK1.2, JACK1.6, JACK1.7, JACK1.8, R20.Pin_1
  N25: JACK1.SHLD2, JACK2.SHLD1, JACK2.SHLD2, JACK3.SHLD1, JACK3.SHLD2, JACK4.SHLD1, JACK4.SHLD2, JACK5.SHLD1, JACK5.SHLD2, JACK6.SHLD1, JACK6.SHLD2, JACK7.SHLD1, JACK7.SHLD2, JACK9.SHLD1, JACK9.SHLD2, JACK10.SHLD1, JACK10.SHLD2, JACK11.SHLD1, JACK11.SHLD2, JACK12.SHLD1, JACK12.SHLD2, JACK13.SHLD1, JACK13.SHLD2, JACK14.SHLD1, JACK14.SHLD2, JACK15.SHLD1, JACK15.SHLD2
  N26: J1.pin2, J2.pin2, 24V.PWR, air_asssist_ssr.pin4, J3.pin2
  N27: J1.pin3, JACK15.1, JACK15.3
  N28: J1.pin4, JACK15.2, JACK15.6
  N29: J1.pin5, JACK15.4, JACK15.8
  N30: J1.pin6, JACK15.5, JACK15.7
  N31: J2.pin3, JACK14.1, JACK14.3
  N32: J2.pin4, JACK14.2, JACK14.6
  N33: J2.pin5, JACK14.4, JACK14.8
  N34: J2.pin6, JACK14.5, JACK14.7
  N35: JACK2.2, JACK2.6, JACK2.8, R23.Pin_1
  N36: IC4.2, R25.Pin_0
  N37: IC4.4, R24.Pin_0
  N38: JACK3.2, JACK3.6, R26.Pin_1
  N39: JACK4.2, JACK4.6, JACK4.8, R24.Pin_1
  N40: JACK5.2, JACK5.6, JACK5.8, R28.Pin_1
  N41: JACK6.2, JACK6.6, R29.Pin_1
  N42: 5V.PWR, JACK7.1, JACK7.3, JACK7.4, JACK7.GLED-, JACK7.GLED+, JACK9.1, JACK9.3, JACK9.GLED-, JACK9.GLED+, JACK10.1, JACK10.3, JACK10.GLED+
  N43: 5V.GND, R21.Pin_1, R22.Pin_1, R25.Pin_1, R27.Pin_1, R30.Pin_1, R31.Pin_1, R47.Pin_1, R49.Pin_1
  N44: JACK7.2, JACK7.5, JACK7.6, JACK7.7, JACK7.8, R48.Pin_1
  N45: JACK9.2, JACK9.5, JACK9.6, JACK9.7, R50.Pin_1
  N46: JACK10.2, JACK10.5, JACK10.6, JACK10.8, R32.Pin_1
  N47: JACK12.1, JACK12.3, IC7.8, R44.Pin_0, air_asssist_ssr1.pin3, C4.1
  N48: JACK12.2, JACK12.6, IC7.6
  N49: JACK12.5, R44.Pin_1, R45.Pin_0, air_asssist_ssr1.pin4
  N50: JACK12.7, JACK12.8, IC7.5, R45.Pin_1, C4.0
  N51: IC7.1, R36.Pin_0
  N52: IC7.2, R43.Pin_0
  N53: IC7.3, R41.Pin_0
  N54: IC7.4, R42.Pin_0
  N55: IC8.3, R40.Pin_0
  N56: IC8.4, R32.Pin_0
  N57: air_asssist_ssr.pin1, R51.Pin_1
  N58: air_asssist_ssr1.pin1, R46.Pin_0
  N59: IC9.1, R48.Pin_0
  N60: IC9.2, R47.Pin_0
  N61: IC9.3, R49.Pin_0
  N62: IC9.4, R50.Pin_0
  N63: J3.pin3, JACK13.1, JACK13.3
  N64: J3.pin4, JACK13.2, JACK13.6
  N65: J3.pin5, JACK13.4, JACK13.8
  N66: J3.pin6, JACK13.5, JACK13.7

notes:
  chiller
  door
  air_assist
  aux1_assist
  x-step
  y-step
  z-step
  x-dir
  y-dir
  z-dir
  5V-TH-TL-WP-G-IN
  laser PSU
  GND
  24V
  24V PSU
  x1-limit
  x2-limit
  y2-limit
  y1-limit
  y-driver
  x-driver
  G201X
  z2-limit
  z1-limit
  door-1
  chiller-in
  laser
  door-2
  air-assist
  5V(wgr1,wor3)-TH(bl4)-TL-WP(gr2,or6)-G(wbr7,br8)-IN(wbl5)
  z-driver
  z-stepper
  y-stepper
  x-stepper

custom parts:
  ETHERNET-JACK-90: RJ-45 with LEDs Perpendicular to PCB Amphenol RJHSE3381A1
